# Fritzing sketch Siren_Schema (saved by Fritzing 0.9.3b)
breadboards: 1

parts:
  NRF24L01+ = NRF24L01+ Breakout Board
  C1 = Electrolytic Capacitor [capacitance=4.7µF package="100 mil [THT, electrolytic]"]
  Arduino1 = Arduino Pro Mini (5V)
  Q1 = Basic FET N-Channel [part_number=IRLZ44N package="D2Pak [SMD]"]
  Power_plug1 = Power plug
  J1 = Screw terminal - 2 pins [part_number=SIREN package=THT]
  U1 = Header 8 [part_number=Keypad package=1x08_smd]
  J2 = Piezo Speaker [part_number=Piezo]
  Power_plug2 = Power plug

nets:
  GND: NRF24L01+.GND, C1.-, Arduino1.GND, Q1.source, Power_plug1.GND, J2.pin2, Power_plug2.GND
  3.3V: NRF24L01+.VCC, C1.+
  CE: NRF24L01+.CE, Arduino1.D9
  CSN: NRF24L01+.CS, Arduino1.D10
  SCK: NRF24L01+.SCK, Arduino1.SCK
  MOSI: NRF24L01+.MOSI, Arduino1.MOSI
  MISO: NRF24L01+.MISO, Arduino1.MISO
  IRQ: NRF24L01+.IRQ, Arduino1.D2
  5V: Arduino1.VCC, Power_plug1.VCC
  PIEZO: Arduino1.A2, J2.pin1
  COL1: Arduino1.A1, U1.1
  SIREN: Arduino1.A0, Q1.Gate
  COL2: Arduino1.D8, U1.2
  COL3: Arduino1.D7, U1.3
  ROW1: Arduino1.D6, U1.4
  ROW2: Arduino1.D5, U1.5
  ROW3: Arduino1.D4, U1.6
  ROW4: Arduino1.D3, U1.7
  N1: Q1.drain, J1.pin2
  12V: J1.pin1, Power_plug2.VCC

notes:
  Siren, V1.0
